// Logisim project Adder.circ as structural Verilog: 3 circuits, main circuit main
module main (
  input  A,
  input  B,
  input  Cin,
  output SumAB,
  output Sum,
  output CAB,
  output Cout,
  output Ctmp
);

  xor xor_1 (SumAB, A, B);
  and and_1 (CAB, A, B);
  and and_2 (Ctmp, SumAB, Cin);
  or or_1 (Cout, CAB, Ctmp);
  xor xor_2 (Sum, SumAB, Cin);

  // Notes on the sheet:
  //   全加器
endmodule

module _1bit_full_adder (
  input  A,
  input  B,
  input  Cin,
  output Sum,
  output Cout
);

  wire and_1_out, and_2_out, xor_1_out;

  xor xor_1 (xor_1_out, A, B);
  and and_1 (and_1_out, A, B);
  and and_2 (and_2_out, xor_1_out, Cin);
  or or_1 (Cout, and_1_out, and_2_out);
  xor xor_2 (Sum, xor_1_out, Cin);
endmodule

module _8bit_ripple_carry_adder (
  input  [7:0] A,
  input  [7:0] B,
  input  Cin,
  output [7:0] Result,
  output Cout
);

  wire n1bit_full_adder_1_cout, n1bit_full_adder_2_cout, n1bit_full_adder_3_cout, n1bit_full_adder_4_cout,
       n1bit_full_adder_5_cout, n1bit_full_adder_6_cout, n1bit_full_adder_7_cout;

  _1bit_full_adder u_1bit_full_adder_1 (.A(A[0]), .B(B[0]), .Cin(Cin), .Sum(Result[0]), .Cout(n1bit_full_adder_1_cout));
  _1bit_full_adder u_1bit_full_adder_2 (
    .A(A[1]), .B(B[1]), .Cin(n1bit_full_adder_1_cout), .Sum(Result[1]), .Cout(n1bit_full_adder_2_cout));
  _1bit_full_adder u_1bit_full_adder_3 (
    .A(A[2]), .B(B[2]), .Cin(n1bit_full_adder_2_cout), .Sum(Result[2]), .Cout(n1bit_full_adder_3_cout));
  _1bit_full_adder u_1bit_full_adder_4 (
    .A(A[4]), .B(B[4]), .Cin(n1bit_full_adder_5_cout), .Sum(Result[4]), .Cout(n1bit_full_adder_4_cout));
  _1bit_full_adder u_1bit_full_adder_5 (
    .A(A[3]), .B(B[3]), .Cin(n1bit_full_adder_3_cout), .Sum(Result[3]), .Cout(n1bit_full_adder_5_cout));
  _1bit_full_adder u_1bit_full_adder_6 (
    .A(A[6]), .B(B[6]), .Cin(n1bit_full_adder_7_cout), .Sum(Result[6]), .Cout(n1bit_full_adder_6_cout));
  _1bit_full_adder u_1bit_full_adder_7 (
    .A(A[5]), .B(B[5]), .Cin(n1bit_full_adder_4_cout), .Sum(Result[5]), .Cout(n1bit_full_adder_7_cout));
  _1bit_full_adder u_1bit_full_adder_8 (
    .A(A[7]), .B(B[7]), .Cin(n1bit_full_adder_6_cout), .Sum(Result[7]), .Cout(Cout));
endmodule
